# Fritzing sketch diagram (saved by Fritzing 0.9.0b)
breadboards: 1

parts:
  Part1 = Arduino Uno (Rev3)
  S2 = Pushbutton [package=THT]
  R1 = Resistor [tolerance=±1% resistance=10k package=THT]

nets:
  N1: Part1.D2, S2.leg1, R1.Pin_0
  N2: Part1.5V, R1.Pin_1
  N3: Part1.GND, S2.leg0
